# Fritzing sketch phase-2-potential (saved by Fritzing 0.9.3b)
breadboards: 1

parts:
  Raspberry_Pi_1 = Raspberry Pi 3 [part_number=RPI-3-V1.2]
  DHT1 = DHT11 Humitidy and Temperature Sensor
  R1 = Resistor [tolerance=±5% resistance=220 package=THT]
  LED1 = LED - 5mm [color="Red (633nm)" package="5 mm [THT]"]
  R2 = Resistor [tolerance=±5% resistance=220 package=THT]
  VCC1 = Battery block 9V
  IC1 = L293D [package=THT]
  M1 = DC Motor

nets:
  N1: Raspberry_Pi_1.GIPO4, IC1.In_2
  N2: Raspberry_Pi_1.GIPO17, DHT1.DATA, R1.Pin_1
  N3: Raspberry_Pi_1.GIPO27, IC1.In_1
  N4: Raspberry_Pi_1.GIPO22, IC1.Enable_1
  3V3: Raspberry_Pi_1.3V3, DHT1.VDD, R1.Pin_0
  GND: Raspberry_Pi_1.GND, DHT1.GND, R2.Pin_0, IC1.0V
  N5: Raspberry_Pi_1.GIPO21, LED1.anode
  N6: Raspberry_Pi_1.5V, IC1.+V
  N7: LED1.cathode, R2.Pin_1
  N8: VCC1.+, IC1.+Vmotor
  N9: IC1.Out_1_(_Controlled_by_Enable_1_), M1.pin_1
  N10: IC1.Out_2_(_Controlled_by_Enable_1_), M1.pin_2

custom parts:
  DHT11 Humitidy and Temperature Sensor: DHT11 Humidity and Temperature Sensor
