# Fritzing sketch phase-2-sketch (saved by Fritzing 0.9.3b)
breadboards: 1

parts:
  Raspberry_Pi_1 = Raspberry Pi 3 [part_number=RPI-3-V1.2]
  DHT1 = DHT11 Humitidy and Temperature Sensor
  R1 = Resistor [tolerance=±5% resistance=220 package=THT]
  LED1 = LED - 5mm [color="Red (633nm)" package="5 mm [THT]"]
  R2 = Resistor [tolerance=±5% resistance=220 package=THT]

nets:
  N1: Raspberry_Pi_1.GIPO17, DHT1.DATA, R1.Pin_1
  3V3: Raspberry_Pi_1.3V3, DHT1.VDD, R1.Pin_0
  GND: Raspberry_Pi_1.GND, DHT1.GND, R2.Pin_0
  N2: Raspberry_Pi_1.GIPO21, LED1.anode
  N3: LED1.cathode, R2.Pin_1

custom parts:
  DHT11 Humitidy and Temperature Sensor: DHT11 Humidity and Temperature Sensor
